# Fritzing sketch Schematic (saved by Fritzing 0.9.3b)
breadboards: 1

parts:
  M1 = MAX30102
  U1 = NodeMCU V1.0
  T1 = LM35 Temperature Sensor [package="TO92 [THT]"]
  LCD1 = LCD screen

nets:
  VIN: M1.VIN, U1.3V3, T1.+Vs, LCD1.VDD
  N1: M1.SCL, U1.D1
  N2: M1.SDA, U1.D2
  GND: M1.GND, U1.GND, T1.GND, LCD1.VSS, LCD1.R/W
  N3: U1.D3, LCD1.RS
  N4: U1.D4, LCD1.E
  N5: U1.D5, LCD1.DB4
  N6: U1.D6, LCD1.DB5
  N7: U1.D7, LCD1.DB6
  N8: U1.D8, LCD1.DB7
  N9: U1.A0, T1.Vout

custom parts:
  MAX30102: Oximeter module using the MAX30102 chip. You may wish to read (and check your module) this post on power problems with these modules: https://reedpaper.wordpress.com/2018/08/22/pulse-oximeter-max30100-max30102-how-to-fix-wrong-board/ . As usual, if you want the mounting holes in pcb, you need to drag a hole over the pad in silkscreen to actually drill the hole (by default they are not drilled)
  NodeMCU V1.0: ESP8266 based NodeMCU
